# Fritzing sketch Esquemaeletrico (saved by Fritzing 0.9.5d)
breadboards: 1

parts:
  Componente1 = Arduino Uno (Rev3)
  M1 = Niren can bus module [package=THT]
  Mod1 = ossoyoo-lora-module
  U1 = POT [package=pot_mammoth]
  U2 = POT [package=pot_mammoth]
  Componente2 = InvenSense MPU6050
  R1 = Resistor [tolerance=±5% resistance=120 package=THT]  # not connected

nets:
  N1: Componente1.A0, U2.A
  N2: Componente1.A1, U1.A
  N3: Componente1.A4/SDA, Componente2.SDA
  N4: Componente1.A5/SCL, Componente2.SCL
  N5: Componente1.D10_PWM/SS, M1.pin3
  N6: Componente1.D11_PWM/MOSI, M1.pin5
  N7: Componente1.D12/MISO, M1.pin4
  N8: Componente1.D13/SCK, M1.pin6
  N9: Componente1.D0/RX, Mod1.TXD
  N10: Componente1.D1/TX, Mod1.RXD
  3V3: Componente1.3V3, Mod1.VCC
  5V: Componente1.5V, M1.pin1, U1.S, U2.E, Componente2.VCC
  GND: Componente1.GND, U1.E, U2.S, Componente2.GND

custom parts:
  Niren can bus module: Niren can bus module availabe on ebay and others. Pcb view assumes that you unsolder the 7 pin header and resolder it on the bottom of the module to connect to the pcb. The two jumpers and the can bus connector remain on the top of the board and don't appear in pcb view.
  ossoyoo-lora-module: Osoyoo Long Distance wireless transceiver Uart LoRa Module.
